// Logisim project regfile-fail.circ as structural Verilog: 1 circuit, main circuit regfile
module regfile (
  input  [4:0] rs1,
  input  [4:0] rs2,
  input  [4:0] rd,
  input  [31:0] Write_Data,
  input  RegWEn,
  input  clk,
  output [31:0] ra,
  output [31:0] sp,
  output [31:0] t0,
  output [31:0] t1,
  output [31:0] t2,
  output [31:0] s0,
  output [31:0] s1,
  output [31:0] a0,
  output [31:0] Read_Data_1,
  output [31:0] Read_Data_2
);

  wire x0_read1, x0_read2, x1_read1, x1_read2, x1_write, x2_read1, x2_read2, x2_write, x3_read1, x3_read2,
       x3_write, x4_read1, x4_read2, x4_write, x5_read1, x5_read2, x5_write, x6_read1, x6_read2, x6_write,
       x7_read1, x7_read2, x7_write, x8_read1, x8_read2, x8_write, x9_read1, x9_read2, x9_write, x10_read1,
       x10_read2, x10_write, x11_read1, x11_read2, x11_write, x12_read1, x12_read2, x12_write, x13_read1,
       x13_read2, x13_write, x14_read1, x14_read2, x14_write, x15_read1, x15_read2, x15_write, x16_read1,
       x16_read2, x16_write, x17_read1, x17_read2, x17_write, x18_read1, x18_read2, x18_write, x19_read1,
       x19_read2, x19_write, x20_read1, x20_read2, x20_write, x21_read1, x21_read2, x21_write, x22_read1,
       x22_read2, x22_write, x23_read1, x23_read2, x23_write, x24_read1, x24_read2, x24_write, x25_read1,
       x25_read2, x25_write, x26_read1, x26_read2, x26_write, x27_read1, x27_read2, x27_write, x28_read1,
       x28_read2, x28_write, x29_read1, x29_read2, x29_write, x30_read1, x30_read2, x30_write, x31_read1,
       x31_read2, x31_write;
  wire [31:0] register_1_q, register_2_q, register_3_q, register_4_q, register_5_q, register_6_q,
       register_7_q, register_13_q, register_14_q, register_15_q, register_16_q, register_17_q,
       register_18_q, register_19_q, register_20_q, register_21_q, register_22_q, register_24_q,
       register_25_q, register_27_q, register_30_q, register_31_q, register_32_q;

  Demultiplexer #(.enable("false"), .select(5)) demultiplexer_1 (
    .out0(x0_read1), .out1(x1_read1), .out2(x2_read1), .out3(x3_read1), .out4(x4_read1), .out5(x5_read1),
    .out6(x6_read1), .out7(x7_read1), .out8(x8_read1), .out9(x9_read1), .out10(x10_read1), .out11(x11_read1),
    .out12(x12_read1), .out13(x13_read1), .out14(x14_read1), .out15(x15_read1), .out16(x16_read1),
    .out17(x17_read1), .out18(x18_read1), .out19(x19_read1), .out20(x20_read1), .out21(x21_read1),
    .out22(x22_read1), .out23(x23_read1), .out24(x24_read1), .out25(x25_read1), .out26(x26_read1),
    .out27(x27_read1), .out28(x28_read1), .out29(x29_read1), .out30(x30_read1), .out31(x31_read1), .in(1'b1),
    .sel(rs1));
  Demultiplexer #(.enable("false"), .select(5)) demultiplexer_2 (
    .out1(x1_write), .out2(x2_write), .out3(x3_write), .out4(x4_write), .out5(x5_write), .out6(x6_write),
    .out7(x7_write), .out8(x8_write), .out9(x9_write), .out10(x10_write), .out11(x11_write),
    .out12(x12_write), .out13(x13_write), .out14(x14_write), .out15(x15_write), .out16(x16_write),
    .out17(x17_write), .out18(x18_write), .out19(x19_write), .out20(x20_write), .out21(x21_write),
    .out22(x22_write), .out23(x23_write), .out24(x24_write), .out25(x25_write), .out26(x26_write),
    .out27(x27_write), .out28(x28_write), .out29(x29_write), .out30(x30_write), .out31(x31_write),
    .in(RegWEn), .sel(rd));  // open: out0
  Demultiplexer #(.enable("false"), .select(5)) demultiplexer_3 (
    .out0(x0_read2), .out1(x1_read2), .out2(x2_read2), .out3(x3_read2), .out4(x4_read2), .out5(x5_read2),
    .out6(x6_read2), .out7(x7_read2), .out8(x8_read2), .out9(x9_read2), .out10(x10_read2), .out11(x11_read2),
    .out12(x12_read2), .out13(x13_read2), .out14(x14_read2), .out15(x15_read2), .out16(x16_read2),
    .out17(x17_read2), .out18(x18_read2), .out19(x19_read2), .out20(x20_read2), .out21(x21_read2),
    .out22(x22_read2), .out23(x23_read2), .out24(x24_read2), .out25(x25_read2), .out26(x26_read2),
    .out27(x27_read2), .out28(x28_read2), .out29(x29_read2), .out30(x30_read2), .out31(x31_read2), .in(1'b1),
    .sel(rs2));
  Register #(.width(32)) register_1 (.D(Write_Data), .en(x18_write), .clk(clk), .Q(register_1_q));  // open: clr
  Register #(.width(32)) register_2 (.D(Write_Data), .en(x20_write), .clk(clk), .Q(register_2_q));  // open: clr
  Register #(.width(32)) register_3 (.D(Write_Data), .en(x22_write), .clk(clk), .Q(register_3_q));  // open: clr
  Register #(.width(32)) register_4 (.D(Write_Data), .en(x24_write), .clk(clk), .Q(register_4_q));  // open: clr
  Register #(.width(32)) register_5 (.D(Write_Data), .en(x26_write), .clk(clk), .Q(register_5_q));  // open: clr
  Register #(.width(32)) register_6 (.D(Write_Data), .en(x28_write), .clk(clk), .Q(register_6_q));  // open: clr
  Register #(.width(32)) register_7 (.D(Write_Data), .en(x30_write), .clk(clk), .Q(register_7_q));  // open: clr
  Register #(.width(32)) register_8 (.D(Write_Data), .en(x2_write), .clk(clk), .Q(sp));  // open: clr
  Register #(.width(32)) register_9 (.D(Write_Data), .en(x4_write), .clk(clk), .Q(sp));  // open: clr
  Register #(.width(32)) register_10 (.D(Write_Data), .en(x6_write), .clk(clk), .Q(t1));  // open: clr
  Register #(.width(32)) register_11 (.D(Write_Data), .en(x8_write), .clk(clk), .Q(s0));  // open: clr
  Register #(.width(32)) register_12 (.D(Write_Data), .en(x10_write), .clk(clk), .Q(a0));  // open: clr
  Register #(.width(32)) register_13 (.D(Write_Data), .en(x16_write), .clk(clk), .Q(register_13_q));  // open: clr
  Register #(.width(32)) register_14 (.D(Write_Data), .en(x12_write), .clk(clk), .Q(register_14_q));  // open: clr
  Demultiplexer #(.enable("false"), .width(32)) demultiplexer_4 (
    .out1(Read_Data_1), .in(register_1_q), .sel(x18_read1));  // open: out0
  Demultiplexer #(.enable("false"), .width(32)) demultiplexer_5 (
    .out1(Read_Data_2), .in(register_2_q), .sel(x20_read2));  // open: out0
  Demultiplexer #(.enable("false"), .width(32)) demultiplexer_6 (
    .out1(Read_Data_1), .in(register_2_q), .sel(x20_read1));  // open: out0
  Demultiplexer #(.enable("false"), .width(32)) demultiplexer_7 (
    .out1(Read_Data_1), .in(register_3_q), .sel(x22_read1));  // open: out0
  Demultiplexer #(.enable("false"), .width(32)) demultiplexer_8 (
    .out1(Read_Data_1), .in(register_4_q), .sel(x24_read1));  // open: out0
  Demultiplexer #(.enable("false"), .width(32)) demultiplexer_9 (
    .out1(Read_Data_2), .in(register_5_q), .sel(x26_read2));  // open: out0
  Demultiplexer #(.enable("false"), .width(32)) demultiplexer_10 (
    .out1(Read_Data_1), .in(register_5_q), .sel(x26_read1));  // open: out0
  Demultiplexer #(.enable("false"), .width(32)) demultiplexer_11 (
    .out1(Read_Data_2), .in(register_6_q), .sel(x28_read2));  // open: out0
  Demultiplexer #(.enable("false"), .width(32)) demultiplexer_12 (
    .out1(Read_Data_1), .in(register_6_q), .sel(x28_read1));  // open: out0
  Demultiplexer #(.enable("false"), .width(32)) demultiplexer_13 (
    .out1(Read_Data_2), .in(register_7_q), .sel(x30_read2));  // open: out0
  Demultiplexer #(.enable("false"), .width(32)) demultiplexer_14 (
    .out1(Read_Data_1), .in(register_7_q), .sel(x30_read1));  // open: out0
  Register #(.width(32)) register_15 (.D({32{1'b0}}), .clk(clk), .Q(register_15_q));  // open: en, clr
  Demultiplexer #(.enable("false"), .width(32)) demultiplexer_15 (
    .out1(Read_Data_1), .in(sp), .sel(x2_read1));  // open: out0
  Demultiplexer #(.enable("false"), .width(32)) demultiplexer_16 (
    .out1(Read_Data_1), .in(sp), .sel(x4_read1));  // open: out0
  Demultiplexer #(.enable("false"), .width(32)) demultiplexer_17 (
    .out1(Read_Data_1), .in(t1), .sel(x6_read1));  // open: out0
  Demultiplexer #(.enable("false"), .width(32)) demultiplexer_18 (
    .out1(Read_Data_1), .in(s0), .sel(x8_read1));  // open: out0
  Demultiplexer #(.enable("false"), .width(32)) demultiplexer_19 (
    .out1(Read_Data_1), .in(a0), .sel(x10_read1));  // open: out0
  Register #(.width(32)) register_16 (.D(Write_Data), .en(x14_write), .clk(clk), .Q(register_16_q));  // open: clr
  Demultiplexer #(.enable("false"), .width(32)) demultiplexer_20 (
    .out1(Read_Data_1), .in(register_13_q), .sel(x16_read1));  // open: out0
  Demultiplexer #(.enable("false"), .width(32)) demultiplexer_21 (
    .out1(Read_Data_2), .in(register_1_q), .sel(x18_read2));  // open: out0
  Demultiplexer #(.enable("false"), .width(32)) demultiplexer_22 (
    .out1(Read_Data_2), .in(register_3_q), .sel(x22_read2));  // open: out0
  Demultiplexer #(.enable("false"), .width(32)) demultiplexer_23 (
    .out1(Read_Data_2), .in(register_4_q), .sel(x24_read2));  // open: out0
  Demultiplexer #(.enable("false"), .width(32)) demultiplexer_24 (
    .out1(Read_Data_2), .in(sp), .sel(x2_read2));  // open: out0
  Demultiplexer #(.enable("false"), .width(32)) demultiplexer_25 (
    .out1(Read_Data_2), .in(sp), .sel(x4_read2));  // open: out0
  Demultiplexer #(.enable("false"), .width(32)) demultiplexer_26 (
    .out1(Read_Data_2), .in(t1), .sel(x6_read2));  // open: out0
  Demultiplexer #(.enable("false"), .width(32)) demultiplexer_27 (
    .out1(Read_Data_2), .in(s0), .sel(x8_read2));  // open: out0
  Demultiplexer #(.enable("false"), .width(32)) demultiplexer_28 (
    .out1(Read_Data_2), .in(a0), .sel(x10_read2));  // open: out0
  Demultiplexer #(.enable("false"), .width(32)) demultiplexer_29 (
    .out1(Read_Data_2), .in(register_14_q), .sel(x12_read2));  // open: out0
  Demultiplexer #(.enable("false"), .width(32)) demultiplexer_30 (
    .out1(Read_Data_1), .in(register_14_q), .sel(x12_read1));  // open: out0
  Demultiplexer #(.enable("false"), .width(32)) demultiplexer_31 (
    .out1(Read_Data_2), .in(register_13_q), .sel(x16_read2));  // open: out0
  Demultiplexer #(.enable("false"), .width(32)) demultiplexer_32 (
    .out1(Read_Data_1), .in(register_15_q), .sel(x0_read1));  // open: out0
  Demultiplexer #(.enable("false"), .width(32)) demultiplexer_33 (
    .out1(Read_Data_2), .in(register_16_q), .sel(x14_read2));  // open: out0
  Demultiplexer #(.enable("false"), .width(32)) demultiplexer_34 (
    .out1(Read_Data_1), .in(register_16_q), .sel(x14_read1));  // open: out0
  Demultiplexer #(.enable("false"), .width(32)) demultiplexer_35 (
    .out1(Read_Data_2), .in(register_15_q), .sel(x0_read2));  // open: out0
  Register #(.width(32)) register_17 (.D(Write_Data), .en(x19_write), .clk(clk), .Q(register_17_q));  // open: clr
  Register #(.width(32)) register_18 (.D(Write_Data), .en(x21_write), .clk(clk), .Q(register_18_q));  // open: clr
  Register #(.width(32)) register_19 (.D(Write_Data), .en(x25_write), .clk(clk), .Q(register_19_q));  // open: clr
  Register #(.width(32)) register_20 (.D(Write_Data), .en(x27_write), .clk(clk), .Q(register_20_q));  // open: clr
  Register #(.width(32)) register_21 (.D(Write_Data), .en(x29_write), .clk(clk), .Q(register_21_q));  // open: clr
  Register #(.width(32)) register_22 (.D(Write_Data), .en(x31_write), .clk(clk), .Q(register_22_q));  // open: clr
  Register #(.width(32)) register_23 (.D(Write_Data), .en(x9_write), .clk(clk), .Q(s1));  // open: clr
  Register #(.width(32)) register_24 (.D(Write_Data), .en(x17_write), .clk(clk), .Q(register_24_q));  // open: clr
  Register #(.width(32)) register_25 (.D(Write_Data), .en(x23_write), .clk(clk), .Q(register_25_q));  // open: clr
  Register #(.width(32)) register_26 (.D(Write_Data), .en(x1_write), .clk(clk), .Q(ra));  // open: clr
  Register #(.width(32)) register_27 (.D(Write_Data), .en(x3_write), .clk(clk), .Q(register_27_q));  // open: clr
  Register #(.width(32)) register_28 (.D(Write_Data), .en(x5_write), .clk(clk), .Q(t0));  // open: clr
  Register #(.width(32)) register_29 (.D(Write_Data), .en(x7_write), .clk(clk), .Q(t2));  // open: clr
  Register #(.width(32)) register_30 (.D(Write_Data), .en(x11_write), .clk(clk), .Q(register_30_q));  // open: clr
  Register #(.width(32)) register_31 (.D(Write_Data), .en(x13_write), .clk(clk), .Q(register_31_q));  // open: clr
  Register #(.width(32)) register_32 (.D(Write_Data), .en(x15_write), .clk(clk), .Q(register_32_q));  // open: clr
  Demultiplexer #(.enable("false"), .width(32)) demultiplexer_36 (
    .out1(Read_Data_1), .in(register_17_q), .sel(x19_read1));  // open: out0
  Demultiplexer #(.enable("false"), .width(32)) demultiplexer_37 (
    .out1(Read_Data_1), .in(register_18_q), .sel(x21_read1));  // open: out0
  Demultiplexer #(.enable("false"), .width(32)) demultiplexer_38 (
    .out1(Read_Data_1), .in(register_19_q), .sel(x25_read1));  // open: out0
  Demultiplexer #(.enable("false"), .width(32)) demultiplexer_39 (
    .out1(Read_Data_1), .in(register_20_q), .sel(x27_read1));  // open: out0
  Demultiplexer #(.enable("false"), .width(32)) demultiplexer_40 (
    .out1(Read_Data_1), .in(register_21_q), .sel(x29_read1));  // open: out0
  Demultiplexer #(.enable("false"), .width(32)) demultiplexer_41 (
    .out1(Read_Data_2), .in(register_22_q), .sel(x31_read2));  // open: out0
  Demultiplexer #(.enable("false"), .width(32)) demultiplexer_42 (
    .out1(Read_Data_1), .in(register_22_q), .sel(x31_read1));  // open: out0
  Demultiplexer #(.enable("false"), .width(32)) demultiplexer_43 (
    .out1(Read_Data_1), .in(s1), .sel(x9_read1));  // open: out0
  Demultiplexer #(.enable("false"), .width(32)) demultiplexer_44 (
    .out1(Read_Data_1), .in(register_24_q), .sel(x17_read1));  // open: out0
  Demultiplexer #(.enable("false"), .width(32)) demultiplexer_45 (
    .out1(Read_Data_2), .in(register_17_q), .sel(x19_read2));  // open: out0
  Demultiplexer #(.enable("false"), .width(32)) demultiplexer_46 (
    .out1(Read_Data_2), .in(register_18_q), .sel(x21_read2));  // open: out0
  Demultiplexer #(.enable("false"), .width(32)) demultiplexer_47 (
    .out1(Read_Data_2), .in(register_25_q), .sel(x23_read2));  // open: out0
  Demultiplexer #(.enable("false"), .width(32)) demultiplexer_48 (
    .out1(Read_Data_1), .in(register_25_q), .sel(x23_read1));  // open: out0
  Demultiplexer #(.enable("false"), .width(32)) demultiplexer_49 (
    .out1(Read_Data_2), .in(register_19_q), .sel(x25_read2));  // open: out0
  Demultiplexer #(.enable("false"), .width(32)) demultiplexer_50 (
    .out1(Read_Data_2), .in(register_20_q), .sel(x27_read2));  // open: out0
  Demultiplexer #(.enable("false"), .width(32)) demultiplexer_51 (
    .out1(Read_Data_2), .in(register_21_q), .sel(x29_read2));  // open: out0
  Demultiplexer #(.enable("false"), .width(32)) demultiplexer_52 (
    .out1(Read_Data_2), .in(ra), .sel(x1_read2));  // open: out0
  Demultiplexer #(.enable("false"), .width(32)) demultiplexer_53 (
    .out1(Read_Data_1), .in(ra), .sel(x1_read1));  // open: out0
  Demultiplexer #(.enable("false"), .width(32)) demultiplexer_54 (
    .out1(Read_Data_1), .in(register_27_q), .sel(x3_read1));  // open: out0
  Demultiplexer #(.enable("false"), .width(32)) demultiplexer_55 (
    .out1(Read_Data_1), .in(t0), .sel(x5_read1));  // open: out0
  Demultiplexer #(.enable("false"), .width(32)) demultiplexer_56 (
    .out1(Read_Data_2), .in(t2), .sel(x7_read2));  // open: out0
  Demultiplexer #(.enable("false"), .width(32)) demultiplexer_57 (
    .out1(Read_Data_1), .in(t2), .sel(x7_read1));  // open: out0
  Demultiplexer #(.enable("false"), .width(32)) demultiplexer_58 (
    .out1(Read_Data_2), .in(s1), .sel(x9_read2));  // open: out0
  Demultiplexer #(.enable("false"), .width(32)) demultiplexer_59 (
    .out1(Read_Data_2), .in(register_30_q), .sel(x11_read2));  // open: out0
  Demultiplexer #(.enable("false"), .width(32)) demultiplexer_60 (
    .out1(Read_Data_1), .in(register_30_q), .sel(x11_read1));  // open: out0
  Demultiplexer #(.enable("false"), .width(32)) demultiplexer_61 (
    .out1(Read_Data_2), .in(register_31_q), .sel(x13_read2));  // open: out0
  Demultiplexer #(.enable("false"), .width(32)) demultiplexer_62 (
    .out1(Read_Data_1), .in(register_31_q), .sel(x13_read1));  // open: out0
  Demultiplexer #(.enable("false"), .width(32)) demultiplexer_63 (
    .out1(Read_Data_2), .in(register_32_q), .sel(x15_read2));  // open: out0
  Demultiplexer #(.enable("false"), .width(32)) demultiplexer_64 (
    .out1(Read_Data_1), .in(register_32_q), .sel(x15_read1));  // open: out0
  Demultiplexer #(.enable("false"), .width(32)) demultiplexer_65 (
    .out1(Read_Data_2), .in(register_24_q), .sel(x17_read2));  // open: out0
  Demultiplexer #(.enable("false"), .width(32)) demultiplexer_66 (
    .out1(Read_Data_2), .in(register_27_q), .sel(x3_read2));  // open: out0
  Demultiplexer #(.enable("false"), .width(32)) demultiplexer_67 (
    .out1(Read_Data_2), .in(t0), .sel(x5_read2));  // open: out0

  // Other names for the same wires on the sheet: read_data1[31:0] = Read_Data_1; read_data2[31:0] = Read_Data_2;
  //   read_reg1[4:0] = rs1; read_reg2[4:0] = rs2; write_en = RegWEn; write_reg[4:0] = rd

  // Notes on the sheet:
  //   INPUTS to your circuit
  //   DON'T CHANGE THE LOCATIONS OF THE INPUTS AND OUTPUTS!
  //   These are DEBUG/TEST outputs from your circuit.
  //   OUTPUTS from your circuit
endmodule
