// Logisim project regfile.circ as structural Verilog: 1 circuit, main circuit regfile
module regfile (
  input  [4:0] rs1,
  input  [4:0] rs2,
  input  [4:0] rd,
  input  [31:0] Write_Data,
  input  RegWEn,
  input  clk,
  output [31:0] ra,
  output [31:0] sp,
  output [31:0] t0,
  output [31:0] t1,
  output [31:0] t2,
  output [31:0] s0,
  output [31:0] s1,
  output [31:0] a0,
  output [31:0] Read_Data_1,
  output [31:0] Read_Data_2
);

  wire a0_read1, a0_read2, a0_write, ra_read1, ra_read2, ra_write, s0_read1, s0_read2, s0_write, s1_read1,
       s1_read2, s1_write, sp_read1, sp_read2, sp_write, t0_read1, t0_read2, t0_write, t1_read1, t1_read2,
       t1_write, t2_read1, t2_read2, t2_write, x0_read1, x0_read2;
  wire [31:0] multiplexer_1_out, multiplexer_2_out, multiplexer_3_out, multiplexer_4_out, multiplexer_5_out,
       multiplexer_6_out, multiplexer_7_out, multiplexer_8_out, register_6_q;

  Demultiplexer #(.enable("false"), .select(5)) demultiplexer_1 (
    .out0(x0_read1), .out1(ra_read1), .out2(sp_read1), .out3(t0_read1), .out4(t1_read1), .out5(t2_read1),
    .out6(s0_read1), .out7(s1_read1), .out8(a0_read1), .in(1'b1), .sel(rs1));  // open: out9, out10, out11, out12, out13, out14, out15, out16, out17, out18, out19, out20, out21, out22, out23, out24, out25, out26, out27, out28, out29, out30, out31
  Demultiplexer #(.enable("false"), .select(5)) demultiplexer_2 (
    .out1(ra_write), .out2(sp_write), .out3(t0_write), .out4(t1_write), .out5(t2_write), .out6(s0_write),
    .out7(s1_write), .out8(a0_write), .in(RegWEn), .sel(rd));  // open: out0, out9, out10, out11, out12, out13, out14, out15, out16, out17, out18, out19, out20, out21, out22, out23, out24, out25, out26, out27, out28, out29, out30, out31
  Demultiplexer #(.enable("false"), .select(5)) demultiplexer_3 (
    .out0(x0_read2), .out1(ra_read2), .out2(sp_read2), .out3(t0_read2), .out4(t1_read2), .out5(t2_read2),
    .out6(s0_read2), .out7(s1_read2), .out8(a0_read2), .in(1'b1), .sel(rs2));  // open: out9, out10, out11, out12, out13, out14, out15, out16, out17, out18, out19, out20, out21, out22, out23, out24, out25, out26, out27, out28, out29, out30, out31
  Multiplexer #(.enable("false"), .width(32)) multiplexer_1 (
    .in0(sp), .in1(Write_Data), .out(multiplexer_1_out), .sel(sp_write));
  Multiplexer #(.enable("false"), .width(32)) multiplexer_2 (
    .in0(t0), .in1(Write_Data), .out(multiplexer_2_out), .sel(t0_write));
  Multiplexer #(.enable("false"), .width(32)) multiplexer_3 (
    .in0(t1), .in1(Write_Data), .out(multiplexer_3_out), .sel(t1_write));
  Register #(.width(32)) register_1 (.D(multiplexer_4_out), .en(ra_write), .clk(clk), .Q(ra));  // open: clr
  Multiplexer #(.enable("false"), .width(32)) multiplexer_4 (
    .in0(ra), .in1(Write_Data), .out(multiplexer_4_out), .sel(ra_write));
  Register #(.width(32)) register_2 (.D(multiplexer_1_out), .en(sp_write), .clk(clk), .Q(sp));  // open: clr
  Register #(.width(32)) register_3 (.D(multiplexer_2_out), .en(t0_write), .clk(clk), .Q(t0));  // open: clr
  Register #(.width(32)) register_4 (.D(multiplexer_3_out), .en(t1_write), .clk(clk), .Q(t1));  // open: clr
  Register #(.width(32)) register_5 (.D(multiplexer_5_out), .en(t2_write), .clk(clk), .Q(t2));  // open: clr
  Multiplexer #(.enable("false"), .width(32)) multiplexer_5 (
    .in0(t2), .in1(Write_Data), .out(multiplexer_5_out), .sel(t2_write));
  Register #(.width(32)) register_6 (.D({32{1'b0}}), .clk(clk), .Q(register_6_q));  // open: en, clr
  Demultiplexer #(.enable("false"), .width(32)) demultiplexer_4 (
    .out1(Read_Data_1), .in(ra), .sel(ra_read1));  // open: out0
  Demultiplexer #(.enable("false"), .width(32)) demultiplexer_5 (
    .out1(Read_Data_1), .in(sp), .sel(sp_read1));  // open: out0
  Demultiplexer #(.enable("false"), .width(32)) demultiplexer_6 (
    .out1(Read_Data_1), .in(t0), .sel(t0_read1));  // open: out0
  Demultiplexer #(.enable("false"), .width(32)) demultiplexer_7 (
    .out1(Read_Data_1), .in(t1), .sel(t1_read1));  // open: out0
  Demultiplexer #(.enable("false"), .width(32)) demultiplexer_8 (
    .out1(Read_Data_1), .in(t2), .sel(t2_read1));  // open: out0
  Demultiplexer #(.enable("false"), .width(32)) demultiplexer_9 (
    .out1(Read_Data_2), .in(ra), .sel(ra_read2));  // open: out0
  Demultiplexer #(.enable("false"), .width(32)) demultiplexer_10 (
    .out1(Read_Data_2), .in(sp), .sel(sp_read2));  // open: out0
  Demultiplexer #(.enable("false"), .width(32)) demultiplexer_11 (
    .out1(Read_Data_2), .in(t0), .sel(t0_read2));  // open: out0
  Demultiplexer #(.enable("false"), .width(32)) demultiplexer_12 (
    .out1(Read_Data_2), .in(t1), .sel(t1_read2));  // open: out0
  Demultiplexer #(.enable("false"), .width(32)) demultiplexer_13 (
    .out1(Read_Data_2), .in(t2), .sel(t2_read2));  // open: out0
  Demultiplexer #(.enable("false"), .width(32)) demultiplexer_14 (
    .out1(Read_Data_1), .in(register_6_q), .sel(x0_read1));  // open: out0
  Demultiplexer #(.enable("false"), .width(32)) demultiplexer_15 (
    .out1(Read_Data_2), .in(register_6_q), .sel(x0_read2));  // open: out0
  Multiplexer #(.enable("false"), .width(32)) multiplexer_6 (
    .in0(s0), .in1(Write_Data), .out(multiplexer_6_out), .sel(s0_write));
  Multiplexer #(.enable("false"), .width(32)) multiplexer_7 (
    .in0(s1), .in1(Write_Data), .out(multiplexer_7_out), .sel(s1_write));
  Multiplexer #(.enable("false"), .width(32)) multiplexer_8 (
    .in0(a0), .in1(Write_Data), .out(multiplexer_8_out), .sel(a0_write));
  Register #(.width(32)) register_7 (.D(multiplexer_6_out), .en(s0_write), .clk(clk), .Q(s0));  // open: clr
  Register #(.width(32)) register_8 (.D(multiplexer_7_out), .en(s1_write), .clk(clk), .Q(s1));  // open: clr
  Register #(.width(32)) register_9 (.D(multiplexer_8_out), .en(a0_write), .clk(clk), .Q(a0));  // open: clr
  Demultiplexer #(.enable("false"), .width(32)) demultiplexer_16 (
    .out1(Read_Data_2), .in(s0), .sel(s0_read2));  // open: out0
  Demultiplexer #(.enable("false"), .width(32)) demultiplexer_17 (
    .out1(Read_Data_1), .in(s0), .sel(s0_read1));  // open: out0
  Demultiplexer #(.enable("false"), .width(32)) demultiplexer_18 (
    .out1(Read_Data_1), .in(s1), .sel(s1_read1));  // open: out0
  Demultiplexer #(.enable("false"), .width(32)) demultiplexer_19 (
    .out1(Read_Data_1), .in(a0), .sel(a0_read1));  // open: out0
  Demultiplexer #(.enable("false"), .width(32)) demultiplexer_20 (
    .out1(Read_Data_2), .in(s1), .sel(s1_read2));  // open: out0
  Demultiplexer #(.enable("false"), .width(32)) demultiplexer_21 (
    .out1(Read_Data_2), .in(a0), .sel(a0_read2));  // open: out0

  // Other names for the same wires on the sheet: read_data1[31:0] = Read_Data_1; read_data2[31:0] = Read_Data_2;
  //   read_reg1[4:0] = rs1; read_reg2[4:0] = rs2; write_en = RegWEn; write_reg[4:0] = rd

  // Notes on the sheet:
  //   INPUTS to your circuit
  //   DON'T CHANGE THE LOCATIONS OF THE INPUTS AND OUTPUTS!
  //   These are DEBUG/TEST outputs from your circuit.
  //   OUTPUTS from your circuit
endmodule
